# Fritzing sketch fire_detection_robot (saved by Fritzing 1.0.4)
breadboards: 2

parts:
  HC-SR04_Sensor_Left = HC-SR04 Ultrasonic Distance Sensor
  MQ-2 = MQ-2 Gas Sensor
  L298N_Left = L298_BRIDGE_DRIVER [package=powerso20]
  DC_Motor_Left = gear-motor
  DC_Motor_Right = gear-motor
  GY-NEO6MV3 = SUP500F [package=sup500f]
  SX1278 = Osoyoo SX1278-ra-02
  LORA_ANTENNA = Antenna  # not connected
  DC-DC_Converter_5V = RioRand LM2596
  DC-DC_Converter_6V_(Left) = RioRand LM2596
  Steering_Servo = Basic Servo
  INA260 = INA 260
  microSD = MicroSD Card Module
  HC-SR04_Sensor_Front = HC-SR04 Ultrasonic Distance Sensor
  HC-SR04_Sensor_Right = HC-SR04 Ultrasonic Distance Sensor
  Εξάρτημα3 = Arduino Mega ADK (Rev3)
  Battery_LiPo = LIPO-2000mAh [package=lipo-2000]
  DC-DC_Converter_6V_(Right) = RioRand LM2596
  L298N_Right = L298_BRIDGE_DRIVER [package=powerso20]

nets:
  VCC: HC-SR04_Sensor_Left.VCC, MQ-2.VCC, L298N_Left.VSS, GY-NEO6MV3.VCC, DC-DC_Converter_5V.Pin_3, Steering_Servo.vcc, microSD.VCC, HC-SR04_Sensor_Front.VCC, HC-SR04_Sensor_Right.VCC, Εξάρτημα3.VIN, L298N_Right.VSS
  N1: HC-SR04_Sensor_Left.TRIG, Εξάρτημα3.D30
  N2: HC-SR04_Sensor_Left.ECHO, Εξάρτημα3.D31
  GND: HC-SR04_Sensor_Left.GND, MQ-2.GND, GY-NEO6MV3.GND, SX1278.GND, Steering_Servo.gnd, microSD.GND, HC-SR04_Sensor_Front.GND, HC-SR04_Sensor_Right.GND, Εξάρτημα3.GND
  N3: MQ-2.AO, Εξάρτημα3.A0
  N4: L298N_Left.GND, DC-DC_Converter_6V_(Left).Pin_4
  N5: L298N_Left.OUT1, DC_Motor_Left.pin_2
  N6: L298N_Left.OUT2, DC_Motor_Left.pin_1
  N7: L298N_Left.VS, DC-DC_Converter_6V_(Left).Pin_3
  N8: L298N_Left.IN1, Εξάρτημα3.D22
  N9: L298N_Left.ENA, Εξάρτημα3.D9_PWM
  N10: L298N_Left.IN2, Εξάρτημα3.D23
  N11: DC_Motor_Right.pin_1, L298N_Right.OUT3
  N12: DC_Motor_Right.pin_2, L298N_Right.OUT4
  N13: GY-NEO6MV3.RX-I, Εξάρτημα3.D1/TX0
  N14: GY-NEO6MV3.TX-O, Εξάρτημα3.D0/RX0
  N15: GY-NEO6MV3.PPS, Εξάρτημα3.D2_PWM
  3.3V: SX1278.3.3V, Εξάρτημα3.3V3
  N16: SX1278.RST, Εξάρτημα3.D39
  N17: SX1278.DIO0, Εξάρτημα3.D41
  N18: SX1278.SCK, Εξάρτημα3.D43
  N19: SX1278.MISO, Εξάρτημα3.D45
  N20: SX1278.MOSI, Εξάρτημα3.D47
  N21: SX1278.NSS, Εξάρτημα3.D49
  N22: DC-DC_Converter_5V.Pin_1, DC-DC_Converter_6V_(Left).Pin_1, INA260.IN-, DC-DC_Converter_6V_(Right).Pin_1
  N23: DC-DC_Converter_5V.Pin_2, DC-DC_Converter_6V_(Left).Pin_2, INA260.GND, Battery_LiPo.-, DC-DC_Converter_6V_(Right).Pin_2
  N24: Steering_Servo.pulse, Εξάρτημα3.D11_PWM
  N25: INA260.SCL, Εξάρτημα3.D21/SCL
  N26: INA260.SDA, Εξάρτημα3.D20/SDA
  N27: INA260.IN+, Battery_LiPo.+
  N28: microSD.MISO, Εξάρτημα3.D50/MISO
  N29: microSD.MOSI, Εξάρτημα3.D51/MOSI
  N30: microSD.SCK, Εξάρτημα3.D52/SCK
  N31: microSD.CS, Εξάρτημα3.D53/SS
  N32: HC-SR04_Sensor_Front.TRIG, Εξάρτημα3.D32
  N33: HC-SR04_Sensor_Front.ECHO, Εξάρτημα3.D33
  N34: HC-SR04_Sensor_Right.TRIG, Εξάρτημα3.D34
  N35: HC-SR04_Sensor_Right.ECHO, Εξάρτημα3.D35
  N36: Εξάρτημα3.D10_PWM, L298N_Right.ENB
  N37: Εξάρτημα3.D24, L298N_Right.IN3
  N38: Εξάρτημα3.D25, L298N_Right.IN4
  N39: DC-DC_Converter_6V_(Right).Pin_3, L298N_Right.VS
  N40: DC-DC_Converter_6V_(Right).Pin_4, L298N_Right.GND

notes:
  GND:Black
  VCC: Red (+5V)
  RX: Yellow (D1)
  TX: Green (D0)
  PPS: Blue (D2)
  GND:Black
  VCC: Red (+5V)
  Trig: Yellow (34)
  Echo: Green (35)
  GND:Black
  VCC: Red (+5V)
  Trig: Yellow (30)
  Echo: Green (31)
  GND:Black
  VCC: Red (+5V)
  Trig: Yellow (32)
  Echo: Green (33)
  **PG6SD**
  GND:Black
  VCC: Red (+5V)
  MISO: Purple (50)
  MOSI: Orange (51)
  SCK: Blue (52)
  CS: Yellow (53)
  **SX1278**
  GND:Black
  VCC: Orange (+3.3V)
  MISO: Purple (45)
  MOSI: Orange (47)
  SCK: Blue (43)
  NSS: Yellow (49)
  RST: Grey (39)
  DIO0: Cyan (41)
  **INA260**
  GND:Black
  Vin+: Red (14,8V)
  Vin-: Red (14,8V)
  SCL: Pink (21)
  SDA: Cyan (20)
  **L298 Left**
  1,10,11,20: Black (IC ground)
  6: Red (H-Bridge Power from DC-DC Left)
  12: Red (IC +5V)
  7,8,9: Orange (22,9,23 - IN1, ENA, IN2)
  **L298 Right**
  1,10,11,20: Black (IC ground)
  6: Red (H-Bridge Power from DC-DC LRight)
  12: Red (IC +5V)
  13,14,15: Purple (24,10,25 - IN3, ENB, IN4)
  **Battery specifications**
  Name: TATTU
  Design: LiPo
  Capacity: 2300mAh
  Voltage: 4S (14.8V)
  Discharge rate: 75C

custom parts:
  MQ-2 Gas Sensor: MQ-2 Gas Sensor module of ZHIYU Sensor Kit
  Osoyoo SX1278-ra-02: Osoyoo Long Distance wireless transceiver Uart LoRa Module.
  INA 260: Rev. B, add copy
